// Digital circuit Missing_pipeline.dig as structural Verilog
module Missing_pipeline (
  input  [3:0] A,
  input  [3:0] B,
  input  Clk,
  output [3:0] Sum
);

  Add #(.Bits(4)) add_1 (.a(A), .b(B), .c_i(1'b0), .s(Sum));  // open: c_o
endmodule

/* Test case:
A B Clk Sum
0 0 C 0
3 4 C 0
0 0 C 7
0 0 C 0
*/
