// Digital circuit combinational_loop.dig as structural Verilog
module combinational_loop (
  input  in_1,
  output out_2
);

  wire not_1_out;

  not not_1 (not_1_out, in_1);
  not not_2 (in_1, not_1_out);

  assign out_2 = in_1;
endmodule
