// Digital circuit empty_tunnel.dig as structural Verilog
module empty_tunnel (
  input  A,
  input  B,
  output Y
);

  and and_1 (Y, A, B);

  // Other names for the same wires on the sheet: T = B
endmodule
