// Digital circuit width_mismatch.dig as structural Verilog
module width_mismatch (
  input  [3:0] In,
  input  B,
  output out_3
);

  and and_1 (out_3, In[0], B);
  // Pins of 1 and 4 bits meet at In
endmodule
