// Digital circuit shifter_width_mismatch.dig as structural Verilog
module shifter_width_mismatch (
  input  [31:0] A,
  input  [31:0] B,
  input  [1:0] S,
  output [31:0] Out
);

  wire [31:0] barrelshifter_1_out, barrelshifter_2_out;

  BarrelShifter #(.Bits(32)) barrelshifter_1 (.in(B), .shift(A[4:0]), .out(barrelshifter_1_out));
  BarrelShifter #(.Bits(32), .barrelShifterMode("arithmetic"), .direction("right")) barrelshifter_2 (
    .in(B), .shift(A[4:0]), .out(barrelshifter_2_out));
  Multiplexer #(.Selector_Bits(2), .Bits(32)) multiplexer_1 (
    .sel(S), .in_0(barrelshifter_1_out), .in_1({32{1'b0}}), .in_2({32{1'b0}}), .in_3(barrelshifter_2_out),
    .out(Out));

  // Other names for the same wires on the sheet: Shamt[4:0] = A[4:0]
endmodule
