// Digital circuit subcircuit_inner.dig as structural Verilog
module subcircuit_inner (
  input  A,
  input  B,
  output Y
);

  wire and_1_out;

  and and_1 (and_1_out, A, B);
  not not_1 (Y, and_1_out);
endmodule
