// Digital circuit pipelined_adder_correct.dig as structural Verilog
module pipelined_adder_correct (
  input  [3:0] A,
  input  [3:0] B,
  input  Clk,
  output [3:0] Sum
);

  wire [3:0] add_1_c_o, RegA1_q, RegB1_q, RegSum2_q;

  Register #(.Bits(4)) RegA1 (.D(A), .C(Clk), .en(1'b1), .Q(RegA1_q));
  Register #(.Bits(4)) RegB1 (.D(B), .C(Clk), .en(1'b1), .Q(RegB1_q));
  Add #(.Bits(4)) add_1 (.a(RegA1_q), .b(RegB1_q), .c_i(1'b1), .c_o(add_1_c_o[0]));  // open: s
  Register #(.Bits(4)) RegSum2 (.D(add_1_c_o), .C(Clk), .en(1'b1), .Q(RegSum2_q));
  Register #(.Bits(4)) u_Sum (.D(RegSum2_q), .C(Clk), .en(1'b1), .Q(Sum));
  // Pins of 1 and 4 bits meet at add_1_c_o
endmodule

/* Test case:
A B Clk Sum
0 0 C 0
3 4 C 0
0 0 C 7
0 0 C 0
*/
